# Fritzing sketch Component Diagram (saved by Fritzing 0.9.3b)
breadboards: 1

parts:
  Part1 = Adafruit Feather HUZZAH ESP8266 [part_number="Adafruit #2821"]
  Q1 = NPN-Transistor [package="TO92 [THT]"]
  Part2 = Lilypad Battery Connect
  U1 = G3VM-61E1 [package=g3vm-61e1]
  R1 = Resistor [tolerance=±5% resistance=220 package="0603 [SMD]"]

nets:
  N1: Part1.GND, Q1.E
  N2: Part1.3.3V, U1.P$5
  N3: Part1.GPIO15, R1.Pin_1
  N4: Q1.B, R1.Pin_0
  N5: Q1.C, U1.P$2
  N6: Part2.-, U1.P$3
  N7: Part2.+, U1.P$6

notes:
  Computer Power
  Relay
  Feather Huzzah
  Transistor
  1 kΩ

custom parts:
  Adafruit Feather HUZZAH ESP8266: his is the Adafruit Feather HUZZAH ESP8266 - our take on an 'all-in-one' ESP8266 WiFi development board with built in USB and battery charging. Its an ESP8266 WiFi module with all the extras you need, ready to rock! We have other boards in the Feather family, check'em out here. At the Feather HUZZAH's heart is an ESP8266 WiFi microcontroller clocked at 80 MHz and at 3.3V logic. This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
